# Fritzing sketch bepid-senac-fritzing-esquematico (saved by Fritzing 0.8.7b)
breadboards: 1

parts:
  Componente1 = Triple Axis Accelerometer Breakout - MMA7361
  Componente2 = Arduino Uno (Rev3)  # not connected
  Componente3 = Arduino Ethernet Shield (Rev3)
  U2 = HC-SR04 [chip_label=IC package="SIP (Single Inline) [THT]"]

nets:
  N1: Componente1.ST, Componente3.D8
  N2: Componente1.GSEL, Componente3.PWM_D6
  N3: Componente1.0GD, Componente3.D7
  N4: Componente1.SLP, Componente3.PWM_D9
  N5: Componente1.XOUT, Componente3.A0
  N6: Componente1.YOUT, Componente3.A1
  N7: Componente1.ZOUT, Componente3.A2
  GND: Componente1.GND, U2.GND
  VCC: Componente1.VCC, U2.Vcc
  N8: Componente3.D2, U2.Trig
  N9: Componente3.SDCS, U2.Echo

custom parts:
  Triple Axis Accelerometer Breakout - MMA7361: Description: This is a breakout board for Freescale's MMA7361L three-axis analog accelerometer. The sensor requires a very low amount of power and has a g-select input which switches the accelerometer between ±1.5g and ±6g measurement ranges. Other features include a sleep mode, signal conditioning, a 1-pole low pass filter, temperature compensation, self test, and 0g-detect which detects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
  HC-SR04: HC-SR04 ultrasound distance sensor
